# Fritzing sketch Clock (saved by Fritzing 0.9.4)
breadboards: 1

parts:
  元件1 = Arduino Uno (Rev3)
  元件2 = Adafruit I2C+SPI LCD Backpack [part_number="Adafruit #292"]
  LCD1 = LCD screen
  RHT1 = Humidity and Temperature Sensor RHT03
  LED1 = RGB LED (com. cathode, rbg) [package="5 mm [THT]"]
  BuzzerDFR1 = BuzzerDFR0032
  元件3 = Real Time Clock Module - DS1307 RTC Breakout Board
  TouchKeyPad1 = TouchKeyPad  # not connected
  J1 = Camdenboss CTB0158-4 [part_number=CTB0158-4 package=THT]  # not connected
  J2 = Camdenboss CTB0158-4 [part_number=CTB0158-4 package=THT]  # not connected

nets:
  N1: 元件1.A0, RHT1.Data-signal
  N2: 元件1.A1, LED1.red_anode
  N3: 元件1.A2, LED1.green_anode
  N4: 元件1.A3, LED1.blue_anode
  N5: 元件1.A4/SDA, 元件2.DATA
  N6: 元件1.A5/SCL, 元件2.CLOCK
  GND: 元件1.GND, 元件2.GND, LCD1.VSS, LCD1.R/W, RHT1.GND_1, BuzzerDFR1.GND, 元件3.GND
  N7: 元件1.D0/RX, BuzzerDFR1.Signal
  N8: 元件1.D2, 元件3.SQW
  N9: 元件1.D3_PWM, 元件3.SDA
  N10: 元件1.D4, 元件3.SCL
  5V: 元件1.5V, 元件2.VCC, LCD1.VDD, LCD1.LED+, RHT1.Vcc, BuzzerDFR1.5V, 元件3.5V
  N11: 元件2.CONTRAST, LCD1.V0
  N12: 元件2.RS, LCD1.RS
  N13: 元件2.E, LCD1.E
  N14: 元件2.DB0, LCD1.DB0
  N15: 元件2.DB1, LCD1.DB1
  N16: 元件2.DB2, LCD1.DB2
  N17: 元件2.DB3, LCD1.DB3
  N18: 元件2.DB4, LCD1.DB4
  N19: 元件2.DB5, LCD1.DB5
  N20: 元件2.DB6, LCD1.DB6
  N21: 元件2.DB7, LCD1.DB7
  N22: 元件2.LEDK, LCD1.LED-

custom parts:
  Adafruit I2C+SPI LCD Backpack: LCD backpacks reduce the number of pins needed to connect to an LCD. LCDs are a fun and easy way to have your microcontroller project talk back to you. Character LCDs are common, and easy to get, available in tons of colors and sizes. We've written tutorials on using character LCDs with an Arduino (or similar microcontroller) but find that the number of pins necessary to control the LCD can be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
